# Fritzing sketch clock (saved by Fritzing 0.9.3b)

parts:
  J2 = Generic female header - 8 pins [form="♀ (female)" package=THT]
  J3 = Generic female header - 6 pins [form="♀ (female)" package=THT]
  J4 = Generic female header - 4 pins [form="♀ (female)" package=THT]

nets:
  N1: J2.pin1, J4.pin3
  N2: J2.pin3, J4.pin2
  N3: J2.pin4, J4.pin1
  N4: J2.pin7, J3.pin4
  N5: J2.pin8, J3.pin3

notes:
  0. Disconnect Arduino from USB
  1. Make connections as on this diagram.
  3. Install "RTClib" by Adafruit
  4. Install "TM1637" by Avishay Orpaz
  6. Make new sketch, copy the clock.ino code in to it.
  7. Load and run.

custom parts:
  Generic female header - 8 pins: Generic female header
  Generic female header - 6 pins: Generic female header
  Generic female header - 4 pins: Generic female header
